# Fritzing sketch circuit_project4 (saved by Fritzing 0.9.2b)
breadboards: 1

parts:
  Part2 = Arduino Uno (Rev3)
  PIR4 = PIR sensor
  U5 = HC-SR04 [chip_label=IC package="SIP (Single Inline) [THT]"]
  LED5 = LED - 5mm [color="Red (660nm)" package="5 mm [THT]"]
  LED6 = LED - 5mm [color="White (6500K)" package="5 mm [THT]"]
  LED7 = LED - 5mm [color="White (6500K)" package="5 mm [THT]"]
  LED8 = LED - 5mm [color="Green (560nm)" package="5 mm [THT]"]
  J1 = Piezo Speaker  # not connected

nets:
  N1: Part2.D11_PWM/MOSI, U5.Trig
  GND: Part2.GND, PIR4.GND, U5.GND, LED5.anode, LED6.anode, LED7.anode, LED8.anode
  N2: Part2.D2, PIR4.SIG
  N3: Part2.D4, LED8.cathode
  N4: Part2.D5_PWM, LED5.cathode
  N5: Part2.D6_PWM, LED6.cathode
  N6: Part2.D7, LED7.cathode
  5V: Part2.5V, PIR4.VDD, U5.Vcc

custom parts:
  HC-SR04: HC-SR04 ultrasound distance sensor
